# Fritzing sketch switchPot (saved by Fritzing 0.9.0b)
circuit board: 8.46667cm x 5.64444cm
breadboards: 1

parts:
  Part1 = Arduino Uno (Rev3)
  R1 = Rotary Potentiometer (Small) [maximum_resistance=100kΩ package=THT]
  S1 = Pushbutton [package="[THT]"]
  S2 = Pushbutton [package="[THT]"]
  S3 = Pushbutton [package="[THT]"]
  S4 = Pushbutton [package="[THT]"]

nets:
  N1: Part1.D8, R1.wiper
  N2: Part1.5V, R1.leg1
  N3: Part1.GND, R1.leg2
  N4: S1.Pin_1, S1.Pin_2
  N5: S1.Pin_3, S1.Pin_4
  N6: S2.Pin_1, S2.Pin_2
  N7: S2.Pin_3, S2.Pin_4
  N8: S3.Pin_1, S3.Pin_2
  N9: S3.Pin_3, S3.Pin_4
  N10: S4.Pin_1, S4.Pin_2
  N11: S4.Pin_3, S4.Pin_4
